# Fritzing sketch breadboard_mosfet (saved by Fritzing 0.9.3b)
breadboards: 2

parts:
  U1 = NodeMCU V1.0
  S2 = Pushbutton [package="[SMD]"]
  YwRobot_Power_Supply1 = YwRobot Breadboard Power Supply [part_number=545043]
  R3 = Resistor [tolerance=±5% resistance=10k package="0805 [SMD]"]
  R10 = Resistor [tolerance=±5% resistance=4.7k package="0805 [SMD]"]
  LED2 = LED - 5mm [color="Blue (505nm)" package="5 mm [THT]"]
  R11 = Resistor [tolerance=±5% resistance=100 package="0805 [SMD]"]
  LED3 = LED - 5mm [color="Green (565nm)" package="5 mm [THT]"]
  R12 = Resistor [tolerance=±5% resistance=100 package="0805 [SMD]"]
  Q2 = Basic FET P-Channel [package="DPak [SMD]"]
  Q3 = Basic FET N-Channel [package="DPak [SMD]"]
  R13 = Resistor [tolerance=±5% resistance=10k package="0805 [SMD]"]
  S3 = Momentary Switch [package=ksa_sealed_tac_switch]

nets:
  N1: U1.D0, U1.3V3, S2.Pin_1, S2.Pin_2, S2.Pin_3, S2.Pin_4, YwRobot_Power_Supply1.VCC#5, R3.Pin_0
  N2: U1.D1, R10.Pin_1, Q3.Gate
  N3: U1.D2, Q2.Gate, R13.Pin_0
  GND: U1.D4, U1.GND, YwRobot_Power_Supply1.GND, R3.Pin_1, R10.Pin_0, LED3.cathode, R12.Pin_1, Q3.source
  N4: U1.Vin, Q2.drain, S3.1, S3.3
  N5: YwRobot_Power_Supply1.VCC#9, LED2.cathode, R11.Pin_1, Q3.drain
  N6: LED2.anode, R11.Pin_0
  N7: LED3.anode, R12.Pin_0
  N8: R13.Pin_1, S3.2, S3.4

notes:
  Q3 - N-Channel MOSFET 30N06L
  https://goo.gl/H49orx
  U2 - Reed-Relais
  https://goo.gl/JOHJuA
  R10 - PullDown
  R11 - Vorwiderstand 5V f. Diode
  3.3 V
  5 V
  S1 Schaltet VIN für den NodeMCU.
  Wenn der NMCU Spannung bekommt schaltet er sich selbst über D2 das Relais U2 ein und versorgt sich damit selbst mit Strom

custom parts:
  NodeMCU V1.0: ESP8266 based NodeMCU
  YwRobot Breadboard Power Supply: The YwRobot Breadboard Power Supply (MB-V2) has two power rails; they can be 5V or 3V3. Power to the module can be provided through the female USB socket or through the A10 (female) 2.1mm power jack.
