# Fritzing sketch breadboard_relais (saved by Fritzing 0.9.3b)
breadboards: 2

parts:
  U1 = NodeMCU V1.0
  S1 = Pushbutton [package="[SMD]"]
  S2 = Pushbutton [package="[SMD]"]
  YwRobot_Power_Supply1 = YwRobot Breadboard Power Supply [part_number=545043]
  R3 = Resistor [tolerance=±5% resistance=10k package="0805 [SMD]"]
  Q1 = MOSFET-NCHANNEL [package=to220v]
  U2 = RELAY-SOLIDSTATE [package=relay-s108t02]
  R10 = Resistor [tolerance=±5% resistance=4.7k package="0805 [SMD]"]
  LED2 = LED - 5mm [color="Blue (505nm)" package="5 mm [THT]"]
  R11 = Resistor [tolerance=±5% resistance=100 package="0805 [SMD]"]
  LED3 = LED - 5mm [color="Green (565nm)" package="5 mm [THT]"]
  R12 = Resistor [tolerance=±5% resistance=100 package="0805 [SMD]"]

nets:
  N1: U1.D0, U1.3V3, S2.Pin_1, S2.Pin_2, S2.Pin_3, S2.Pin_4, YwRobot_Power_Supply1.VCC#5, R3.Pin_0
  N2: U1.D1, Q1.G, R10.Pin_1
  N3: U1.D2, U2.T2
  N4: U1.D4, R12.Pin_1
  GND: U1.GND, YwRobot_Power_Supply1.GND, R3.Pin_1, Q1.S, U2.+, R10.Pin_0, LED3.cathode
  N5: U1.Vin, S1.Pin_1, S1.Pin_2, S1.Pin_3, S1.Pin_4, YwRobot_Power_Supply1.VCC#9, U2.T1, U2.-, R11.Pin_1
  N6: Q1.D, LED2.cathode
  N7: LED2.anode, R11.Pin_0
  N8: LED3.anode, R12.Pin_0

notes:
  Q1 - N-Channel MOSFET 30N06L
  https://goo.gl/H49orx
  U2 - Reed-Relais
  https://goo.gl/JOHJuA
  R10 - PullDown
  R11 - Vorwiderstand 5V f. Diode
  3.3 V
  5 V
  S1 Schaltet VIN für den NodeMCU.
  Wenn der NMCU Spannung bekommt schaltet er sich selbst über D2 das Relais U2 ein und versorgt sich damit selbst mit Strom

custom parts:
  NodeMCU V1.0: ESP8266 based NodeMCU
  YwRobot Breadboard Power Supply: The YwRobot Breadboard Power Supply (MB-V2) has two power rails; they can be 5V or 3V3. Power to the module can be provided through the female USB socket or through the A10 (female) 2.1mm power jack.
